// Logisim project ESF.circ as structural Verilog: 13 circuits, main circuit RAMfinalfile
module main (
  input  in_1,
  input  [15:0] in_2,
  input  [31:0] in_3,
  input  [31:0] in_4,
  input  [31:0] R0,
  input  [31:0] L0,
  output out_7,
  output [31:0] out_8,
  output [31:0] out_9
);

  wire and_1_out, nand_1_out, or_1_out;
  wire [4:0] counter_1_q;
  wire [15:0] esfkeyschedules_1_out_5, multiplexer_1_out, register_1_q;
  wire [31:0] esfkeyschedules_1_out_6, esfkeyschedules_1_out_7, multiplexer_2_out, multiplexer_3_out,
       multiplexer_4_out, multiplexer_5_out, n7shifteresf_1_out_2, register_2_q, register_3_q, register_4_q,
       register_5_q, serpentsboxlayers_1_out_2, xor_1_out, xor_2_out;

  or or_1 (or_1_out, counter_1_q[0], counter_1_q[1], counter_1_q[2], counter_1_q[3], counter_1_q[4]);
  Multiplexer #(.width(16), .enable("false")) multiplexer_1 (
    .in0(in_2), .in1(register_1_q), .out(multiplexer_1_out), .sel(or_1_out));
  Multiplexer #(.width(32), .enable("false")) multiplexer_2 (
    .in0(in_3), .in1(register_2_q), .out(multiplexer_2_out), .sel(or_1_out));
  Multiplexer #(.width(32), .enable("false")) multiplexer_3 (
    .in0(in_4), .in1(register_3_q), .out(multiplexer_3_out), .sel(or_1_out));
  Multiplexer #(.width(32), .enable("false")) multiplexer_4 (
    .in0(R0), .in1(register_4_q), .out(multiplexer_4_out), .sel(or_1_out));
  Multiplexer #(.width(32), .enable("false")) multiplexer_5 (
    .in0(L0), .in1(register_5_q), .out(multiplexer_5_out), .sel(or_1_out));
  Counter #(.width(5), .max('h1f), .ongoal("stay")) counter_1 (
    .Q(counter_1_q), .carry(out_7), .clk(in_1));  // open: load, D, count, clr
  assign xor_1_out = multiplexer_3_out ^ multiplexer_4_out;  // XOR_Gate xor_1, 32 bits wide
  serpentsboxlayers serpentsboxlayers_1 (.in_1(xor_1_out), .out_2(serpentsboxlayers_1_out_2));
  _7SHIFTERESF u_7shifteresf_1 (.in_1(multiplexer_5_out), .out_2(n7shifteresf_1_out_2));
  ESFkeyschedules esfkeyschedules_1 (
    .in_2(multiplexer_1_out), .in_3(multiplexer_2_out), .in_4(multiplexer_3_out), .in_1(counter_1_q),
    .out_5(esfkeyschedules_1_out_5), .out_6(esfkeyschedules_1_out_6), .out_7(esfkeyschedules_1_out_7));
  assign xor_2_out = serpentsboxlayers_1_out_2 ^ n7shifteresf_1_out_2;  // XOR_Gate xor_2, 32 bits wide
  nand nand_1 (nand_1_out, counter_1_q[0], counter_1_q[1], counter_1_q[2], counter_1_q[3], counter_1_q[4]);
  Register #(.width(16)) register_1 (
    .D(esfkeyschedules_1_out_5), .en(nand_1_out), .Q(register_1_q), .clk(in_1));  // open: clr
  Register #(.width(32)) register_2 (
    .D(esfkeyschedules_1_out_6), .en(nand_1_out), .Q(register_2_q), .clk(in_1));  // open: clr
  Register #(.width(32)) register_3 (
    .D(esfkeyschedules_1_out_7), .en(nand_1_out), .Q(register_3_q), .clk(in_1));  // open: clr
  Register #(.width(32)) register_4 (.D(xor_2_out), .en(nand_1_out), .Q(register_4_q), .clk(in_1));  // open: clr
  Register #(.width(32)) register_5 (
    .D(multiplexer_4_out), .en(nand_1_out), .Q(register_5_q), .clk(in_1));  // open: clr
  Multiplexer #(.width(32), .enable("false")) multiplexer_6 (
    .in1(xor_2_out), .out(out_8), .sel(and_1_out));  // open: in0
  Multiplexer #(.width(32), .enable("false")) multiplexer_7 (
    .in1(multiplexer_4_out), .out(out_9), .sel(and_1_out));  // open: in0
  and and_1 (and_1_out, counter_1_q[0], counter_1_q[1], counter_1_q[2], counter_1_q[3], counter_1_q[4]);

  // Notes on the sheet:
  //   MSB
  //   LSB
endmodule

module _7SHIFTERESF (
  input  [31:0] in_1,
  output [31:0] out_2
);


  assign out_2 = {in_1[24:0], in_1[31:25]};
endmodule

module SBOX0 (
  input  LSB,
  input  in_2,
  input  in_3,
  input  MSB,
  output out_5,
  output out_6,
  output out_7,
  output out_8
);

  Multiplexer #(.select(4), .width(4)) multiplexer_1 (
    .in0(4'b0011), .in1(4'b1000), .in2(4'b1111), .in3(4'b0001), .in4(4'b1010), .in5(4'b0110), .in6(4'b0101),
    .in7(4'b1011), .in8(4'b1110), .in9(4'b1101), .in10(4'b0100), .in11(4'b0010), .in12(4'b0111),
    .in13(4'b0000), .in14(4'b1001), .in15(4'b1100), .out({out_8, out_7, out_6, out_5}),
    .sel({MSB, in_3, in_2, LSB}));  // open: en
endmodule

module SBOX1 (
  input  D,
  input  C,
  input  B,
  input  A,
  output out_5,
  output out_6,
  output out_7,
  output out_8
);

  wire and_1_out, and_2_out, and_3_out, and_4_out, and_5_out, and_6_out, and_7_out, and_8_out, and_9_out,
       and_10_out, and_11_out, and_12_out, and_13_out, and_14_out, and_15_out, and_16_out, and_17_out,
       and_18_out, and_19_out, and_20_out, and_21_out, not_1_out, not_2_out, not_3_out, not_4_out;

  not not_1 (not_1_out, D);
  not not_2 (not_2_out, C);
  not not_3 (not_3_out, B);
  not not_4 (not_4_out, A);
  and and_1 (and_1_out, not_4_out, not_2_out, not_1_out);
  and and_2 (and_2_out, not_3_out, not_2_out, not_1_out);
  and and_3 (and_3_out, B, C, not_1_out);
  and and_4 (and_4_out, A, not_2_out, D);
  and and_5 (and_5_out, not_4_out, not_3_out, C, D);
  and and_6 (and_6_out, not_4_out, not_3_out, not_1_out);
  and and_7 (and_7_out, not_3_out, C, not_1_out);
  and and_8 (and_8_out, not_4_out, C, D);
  and and_9 (and_9_out, A, B, not_1_out);
  and and_10 (and_10_out, A, not_3_out, not_2_out, D);
  and and_11 (and_11_out, not_4_out, not_3_out, not_2_out);
  and and_12 (and_12_out, not_4_out, not_3_out, D);
  and and_13 (and_13_out, A, B, not_2_out);
  and and_14 (and_14_out, A, B, D);
  and and_15 (and_15_out, not_4_out, B, C, not_1_out);
  and and_16 (and_16_out, A, not_3_out, C, not_1_out);
  and and_17 (and_17_out, not_4_out, not_3_out, not_2_out);
  and and_18 (and_18_out, not_4_out, not_2_out, not_1_out);
  and and_19 (and_19_out, A, not_2_out, D);
  and and_20 (and_20_out, A, not_3_out, C);
  and and_21 (and_21_out, not_4_out, B, C, D);
  or or_1 (out_5, and_1_out, and_2_out, and_3_out, and_4_out, and_5_out);
  or or_2 (out_6, and_6_out, and_7_out, and_8_out, and_9_out, and_10_out);
  or or_3 (out_7, and_11_out, and_12_out, and_13_out, and_14_out, and_15_out, and_16_out);
  or or_4 (out_8, and_17_out, and_18_out, and_19_out, and_20_out, and_21_out);
endmodule

module SBOX2 (
  input  LSB,
  input  in_2,
  input  in_3,
  input  MSB,
  output out_5,
  output out_6,
  output out_7,
  output out_8
);

  Multiplexer #(.select(4), .width(4)) multiplexer_1 (
    .in0(4'b1000), .in1(4'b0110), .in2(4'b0111), .in3(4'b1001), .in4(4'b0011), .in5(4'b1100), .in6(4'b1010),
    .in7(4'b1111), .in8(4'b1101), .in9(4'b0001), .in10(4'b1110), .in11(4'b0100), .in12(4'b0000),
    .in13(4'b1011), .in14(4'b0101), .in15(4'b0010), .out({out_8, out_7, out_6, out_5}),
    .sel({MSB, in_3, in_2, LSB}));  // open: en
endmodule

module SBOX3 (
  input  LSB,
  input  in_2,
  input  in_3,
  input  MSB,
  output out_5,
  output out_6,
  output out_7,
  output out_8
);

  Multiplexer #(.select(4), .width(4)) multiplexer_1 (
    .in0(4'b0000), .in1(4'b1111), .in2(4'b1011), .in3(4'b1000), .in4(4'b1100), .in5(4'b1001), .in6(4'b0110),
    .in7(4'b0011), .in8(4'b1101), .in9(4'b0001), .in10(4'b0010), .in11(4'b0100), .in12(4'b1010),
    .in13(4'b0111), .in14(4'b0101), .in15(4'b1110), .out({out_8, out_7, out_6, out_5}),
    .sel({MSB, in_3, in_2, LSB}));  // open: en
endmodule

module SBOX4 (
  input  LSB,
  input  in_2,
  input  in_3,
  input  MSB,
  output out_5,
  output out_6,
  output out_7,
  output out_8
);

  Multiplexer #(.select(4), .width(4)) multiplexer_1 (
    .in0(4'b0001), .in1(4'b1111), .in2(4'b1000), .in3(4'b0011), .in4(4'b1100), .in5(4'b0000), .in6(4'b1011),
    .in7(4'b0110), .in8(4'b0010), .in9(4'b0101), .in10(4'b0100), .in11(4'b1010), .in12(4'b1001),
    .in13(4'b1110), .in14(4'b0111), .in15(4'b1101), .out({out_8, out_7, out_6, out_5}),
    .sel({MSB, in_3, in_2, LSB}));  // open: en
endmodule

module SBOX5 (
  input  LSB,
  input  in_2,
  input  in_3,
  input  MSB,
  output out_5,
  output out_6,
  output out_7,
  output out_8
);

  Multiplexer #(.select(4), .width(4)) multiplexer_1 (
    .in0(4'b1111), .in1(4'b0101), .in2(4'b0010), .in3(4'b1011), .in4(4'b0100), .in5(4'b1010), .in6(4'b1001),
    .in7(4'b1100), .in8(4'b0000), .in9(4'b0011), .in10(4'b1110), .in11(4'b1000), .in12(4'b1101),
    .in13(4'b0110), .in14(4'b0111), .in15(4'b0001), .out({out_8, out_7, out_6, out_5}),
    .sel({MSB, in_3, in_2, LSB}));  // open: en
endmodule

module SBOX6 (
  input  LSB,
  input  in_2,
  input  in_3,
  input  MSB,
  output out_5,
  output out_6,
  output out_7,
  output out_8
);

  Multiplexer #(.select(4), .width(4)) multiplexer_1 (
    .in0(4'b0111), .in1(4'b0010), .in2(4'b1100), .in3(4'b0101), .in4(4'b1000), .in5(4'b0100), .in6(4'b0110),
    .in7(4'b1011), .in8(4'b1110), .in9(4'b1001), .in10(4'b0001), .in11(4'b1111), .in12(4'b1101),
    .in13(4'b0011), .in14(4'b1010), .in15(4'b0000), .out({out_8, out_7, out_6, out_5}),
    .sel({MSB, in_3, in_2, LSB}));  // open: en
endmodule

module SBOX7 (
  input  LSB,
  input  in_2,
  input  in_3,
  input  MSB,
  output out_5,
  output out_6,
  output out_7,
  output out_8
);

  Multiplexer #(.select(4), .width(4)) multiplexer_1 (
    .in0(4'b0001), .in1(4'b1101), .in2(4'b1111), .in3(4'b0000), .in4(4'b1110), .in5(4'b1000), .in6(4'b0010),
    .in7(4'b1011), .in8(4'b0111), .in9(4'b0100), .in10(4'b1100), .in11(4'b1010), .in12(4'b1001),
    .in13(4'b0011), .in14(4'b0101), .in15(4'b0110), .out({out_8, out_7, out_6, out_5}),
    .sel({MSB, in_3, in_2, LSB}));  // open: en
endmodule

module ESFkeyschedules (
  input  [4:0] in_1,
  input  [15:0] in_2,
  input  [31:0] in_3,
  input  [31:0] in_4,
  output [15:0] out_5,
  output [31:0] out_6,
  output [31:0] out_7
);

  wire [4:0] adder_1_out;

  Adder #(.width(5)) adder_1 (.a(in_1), .b(5'b00001), .out(adder_1_out));  // open: cin, cout
  SBOX0 sbox0_1 (
    .LSB(in_4[11]), .in_2(in_4[12]), .in_3(in_4[13]), .MSB(in_4[14]), .out_5(out_7[24]), .out_6(out_7[25]),
    .out_7(out_7[26]), .out_8(out_7[27]));
  SBOX0 sbox0_2 (
    .LSB(in_4[15]), .in_2(in_4[16]), .in_3(in_4[17]), .MSB(in_4[18]), .out_5(out_7[28]), .out_6(out_7[29]),
    .out_7(out_7[30]), .out_8(out_7[31]));
  assign out_6[31:27] = adder_1_out ^ in_3[18:14];  // XOR_Gate xor_1, 5 bits wide

  assign out_5 = {in_2[2:0], in_4[31:19]};
  assign out_6[26:0] = {in_3[13:0], in_2[15:3]};
  assign out_7[23:0] = {in_4[10:0], in_3[31:19]};
endmodule

module serpentsboxlayers (
  input  [31:0] in_1,
  output [31:0] out_2
);

  SBOX0 sbox0_1 (
    .LSB(in_1[0]), .in_2(in_1[1]), .in_3(in_1[2]), .MSB(in_1[3]), .out_5(out_2[0]), .out_6(out_2[8]),
    .out_7(out_2[16]), .out_8(out_2[24]));
  SBOX1 sbox1_1 (
    .D(in_1[4]), .C(in_1[5]), .B(in_1[6]), .A(in_1[7]), .out_5(out_2[1]), .out_6(out_2[9]),
    .out_7(out_2[17]), .out_8(out_2[25]));
  SBOX2 sbox2_1 (
    .LSB(in_1[8]), .in_2(in_1[9]), .in_3(in_1[10]), .MSB(in_1[11]), .out_5(out_2[2]), .out_6(out_2[10]),
    .out_7(out_2[18]), .out_8(out_2[26]));
  SBOX3 sbox3_1 (
    .LSB(in_1[12]), .in_2(in_1[13]), .in_3(in_1[14]), .MSB(in_1[15]), .out_5(out_2[3]), .out_6(out_2[11]),
    .out_7(out_2[19]), .out_8(out_2[27]));
  SBOX4 sbox4_1 (
    .LSB(in_1[16]), .in_2(in_1[17]), .in_3(in_1[18]), .MSB(in_1[19]), .out_5(out_2[4]), .out_6(out_2[12]),
    .out_7(out_2[20]), .out_8(out_2[28]));
  SBOX5 sbox5_1 (
    .LSB(in_1[20]), .in_2(in_1[21]), .in_3(in_1[22]), .MSB(in_1[23]), .out_5(out_2[5]), .out_6(out_2[13]),
    .out_7(out_2[21]), .out_8(out_2[29]));
  SBOX6 sbox6_1 (
    .LSB(in_1[24]), .in_2(in_1[25]), .in_3(in_1[26]), .MSB(in_1[27]), .out_5(out_2[6]), .out_6(out_2[14]),
    .out_7(out_2[22]), .out_8(out_2[30]));
  SBOX7 sbox7_1 (
    .LSB(in_1[28]), .in_2(in_1[29]), .in_3(in_1[30]), .MSB(in_1[31]), .out_5(out_2[7]), .out_6(out_2[15]),
    .out_7(out_2[23]), .out_8(out_2[31]));
endmodule

module RAMfinalfile (
  output [31:0] out_1,
  output [31:0] out_2,
  output halt
);

  wire and_1_out, clock_1_out;
  wire [1:0] counter_1_q;
  wire [31:0] ram_1_data, ram_2_data, ram_3_data, ram_4_data, ram_5_data;

  Clock clock_1 (.out(clock_1_out));
  RAM #(.addrWidth(3), .dataWidth(32)) ram_1 (
    .addr(3'b010), .data(ram_1_data), .clk(clock_1_out));  // open: sel, ld, clr
  RAM #(.addrWidth(3), .dataWidth(32)) ram_2 (
    .addr(3'b011), .data(ram_2_data), .clk(clock_1_out));  // open: sel, ld, clr
  RAM #(.addrWidth(3), .dataWidth(32)) ram_3 (
    .addr(3'b100), .data(ram_3_data), .clk(clock_1_out));  // open: sel, ld, clr
  Counter #(.width(2), .max('h3)) counter_1 (.Q(counter_1_q), .clk(clock_1_out));  // open: load, D, count, carry, clr
  RAM #(.addrWidth(3), .dataWidth(32)) ram_4 (
    .addr(3'b000), .data(ram_4_data), .clk(clock_1_out));  // open: sel, ld, clr
  RAM #(.addrWidth(3), .dataWidth(32)) ram_5 (
    .addr(3'b001), .data(ram_5_data), .clk(clock_1_out));  // open: sel, ld, clr
  and and_1 (and_1_out, counter_1_q[1], clock_1_out);
  main main_1 (
    .in_1(and_1_out), .in_2(ram_1_data[15:0]), .in_3({ram_2_data[15:0], ram_1_data[31:16]}),
    .in_4({ram_3_data[15:0], ram_2_data[31:16]}), .R0(ram_4_data), .L0(ram_5_data), .out_7(halt),
    .out_8(out_1), .out_9(out_2));
endmodule
