// Logisim project PRESENT.circ as structural Verilog: 5 circuits, main circuit Ramvala
module main (
  input  in_1,
  input  [15:0] in_2,
  input  [31:0] in_3,
  input  [31:0] in_4,
  input  [31:0] in_5,
  input  [31:0] in_6,
  output out_7,
  output [31:0] out_8,
  output [31:0] out_9
);

  wire and_1_out, nand_1_out, or_1_out;
  wire [4:0] counter_1_q;
  wire [15:0] keytransform_1_out_5, multiplexer_1_out, register_1_q;
  wire [31:0] keytransform_1_out_6, keytransform_1_out_7, multiplexer_2_out, multiplexer_3_out,
       multiplexer_4_out, multiplexer_5_out, register_2_q, register_3_q, register_4_q, register_5_q,
       s_layer_1_out_3, s_layer_1_out_4, xor_1_out, xor_2_out, xor_3_out, xor_4_out;

  assign xor_1_out = in_3 ^ in_5;  // XOR_Gate xor_1, 32 bits wide
  assign xor_2_out = in_4 ^ in_6;  // XOR_Gate xor_2, 32 bits wide
  or or_1 (or_1_out, counter_1_q[0], counter_1_q[1], counter_1_q[2], counter_1_q[3], counter_1_q[4]);
  Multiplexer #(.width(16), .enable("false")) multiplexer_1 (
    .in0(in_2), .in1(register_1_q), .out(multiplexer_1_out), .sel(or_1_out));
  Multiplexer #(.width(32), .enable("false")) multiplexer_2 (
    .in0(in_3), .in1(register_2_q), .out(multiplexer_2_out), .sel(or_1_out));
  Multiplexer #(.width(32), .enable("false")) multiplexer_3 (
    .in0(in_4), .in1(register_3_q), .out(multiplexer_3_out), .sel(or_1_out));
  Multiplexer #(.width(32), .enable("false")) multiplexer_4 (
    .in0(xor_1_out), .in1(register_4_q), .out(multiplexer_4_out), .sel(or_1_out));
  Multiplexer #(.width(32), .enable("false")) multiplexer_5 (
    .in0(xor_2_out), .in1(register_5_q), .out(multiplexer_5_out), .sel(or_1_out));
  keyTRANSFORM keytransform_1 (
    .in_2(multiplexer_1_out), .in_3(multiplexer_2_out), ._48_79(multiplexer_3_out), .in_1(counter_1_q),
    .out_5(keytransform_1_out_5), .out_6(keytransform_1_out_6), .out_7(keytransform_1_out_7));
  S_LAYER s_layer_1 (
    .in_1(multiplexer_4_out), .in_2(multiplexer_5_out), .out_3(s_layer_1_out_3), .out_4(s_layer_1_out_4));
  Counter #(.width(5), .max('h1f), .ongoal("stay")) counter_1 (
    .Q(counter_1_q), .carry(out_7), .clk(in_1));  // open: load, D, count, clr
  assign xor_3_out = keytransform_1_out_6 ^ s_layer_1_out_3;  // XOR_Gate xor_3, 32 bits wide
  assign xor_4_out = keytransform_1_out_7 ^ s_layer_1_out_4;  // XOR_Gate xor_4, 32 bits wide
  nand nand_1 (nand_1_out, counter_1_q[0], counter_1_q[1], counter_1_q[2], counter_1_q[3], counter_1_q[4]);
  Register #(.width(16)) register_1 (
    .D(keytransform_1_out_5), .en(nand_1_out), .Q(register_1_q), .clk(in_1));  // open: clr
  Register #(.width(32)) register_2 (
    .D(keytransform_1_out_6), .en(nand_1_out), .Q(register_2_q), .clk(in_1));  // open: clr
  Register #(.width(32)) register_3 (
    .D(keytransform_1_out_7), .en(nand_1_out), .Q(register_3_q), .clk(in_1));  // open: clr
  Register #(.width(32)) register_4 (.D(xor_3_out), .en(nand_1_out), .Q(register_4_q), .clk(in_1));  // open: clr
  Register #(.width(32)) register_5 (.D(xor_4_out), .en(nand_1_out), .Q(register_5_q), .clk(in_1));  // open: clr
  and and_1 (and_1_out, counter_1_q[0], counter_1_q[1], counter_1_q[2], counter_1_q[3], counter_1_q[4]);
  Multiplexer #(.width(32), .enable("false")) multiplexer_6 (
    .in1(register_5_q), .out(out_8), .sel(and_1_out));  // open: in0
  Multiplexer #(.width(32), .enable("false")) multiplexer_7 (
    .in1(register_4_q), .out(out_9), .sel(and_1_out));  // open: in0

  // Notes on the sheet:
  //   LSB key
  //   MSB key
  //   LSB text
  //   MSB text
endmodule

module SBOX (
  input  LSB,
  input  in_2,
  input  in_3,
  input  MSB,
  output out_5,
  output out_6,
  output out_7,
  output out_8
);

  Multiplexer #(.select(4), .width(4)) multiplexer_1 (
    .in0(4'b1100), .in1(4'b0101), .in2(4'b0110), .in3(4'b1011), .in4(4'b1001), .in5(4'b0000), .in6(4'b1010),
    .in7(4'b1101), .in8(4'b0011), .in9(4'b1110), .in10(4'b1111), .in11(4'b1000), .in12(4'b0100),
    .in13(4'b0111), .in14(4'b0001), .in15(4'b0010), .out({out_8, out_7, out_6, out_5}),
    .sel({MSB, in_3, in_2, LSB}));  // open: en
endmodule

module S_LAYER (
  input  [31:0] in_1,
  input  [31:0] in_2,
  output [31:0] out_3,
  output [31:0] out_4
);

  SBOX sbox_1 (
    .LSB(in_1[0]), .in_2(in_1[1]), .in_3(in_1[2]), .MSB(in_1[3]), .out_5(out_3[0]), .out_6(out_3[16]),
    .out_7(out_4[0]), .out_8(out_4[16]));
  SBOX sbox_2 (
    .LSB(in_1[4]), .in_2(in_1[5]), .in_3(in_1[6]), .MSB(in_1[7]), .out_5(out_3[1]), .out_6(out_3[17]),
    .out_7(out_4[1]), .out_8(out_4[17]));
  SBOX sbox_3 (
    .LSB(in_1[8]), .in_2(in_1[9]), .in_3(in_1[10]), .MSB(in_1[11]), .out_5(out_3[2]), .out_6(out_3[18]),
    .out_7(out_4[2]), .out_8(out_4[18]));
  SBOX sbox_4 (
    .LSB(in_1[12]), .in_2(in_1[13]), .in_3(in_1[14]), .MSB(in_1[15]), .out_5(out_3[3]), .out_6(out_3[19]),
    .out_7(out_4[3]), .out_8(out_4[19]));
  SBOX sbox_5 (
    .LSB(in_1[16]), .in_2(in_1[17]), .in_3(in_1[18]), .MSB(in_1[19]), .out_5(out_3[4]), .out_6(out_3[20]),
    .out_7(out_4[4]), .out_8(out_4[20]));
  SBOX sbox_6 (
    .LSB(in_1[20]), .in_2(in_1[21]), .in_3(in_1[22]), .MSB(in_1[23]), .out_5(out_3[5]), .out_6(out_3[21]),
    .out_7(out_4[5]), .out_8(out_4[21]));
  SBOX sbox_7 (
    .LSB(in_1[24]), .in_2(in_1[25]), .in_3(in_1[26]), .MSB(in_1[27]), .out_5(out_3[6]), .out_6(out_3[22]),
    .out_7(out_4[6]), .out_8(out_4[22]));
  SBOX sbox_8 (
    .LSB(in_1[28]), .in_2(in_1[29]), .in_3(in_1[30]), .MSB(in_1[31]), .out_5(out_3[7]), .out_6(out_3[23]),
    .out_7(out_4[7]), .out_8(out_4[23]));
  SBOX sbox_9 (
    .LSB(in_2[0]), .in_2(in_2[1]), .in_3(in_2[2]), .MSB(in_2[3]), .out_5(out_3[8]), .out_6(out_3[24]),
    .out_7(out_4[8]), .out_8(out_4[24]));
  SBOX sbox_10 (
    .LSB(in_2[4]), .in_2(in_2[5]), .in_3(in_2[6]), .MSB(in_2[7]), .out_5(out_3[9]), .out_6(out_3[25]),
    .out_7(out_4[9]), .out_8(out_4[25]));
  SBOX sbox_11 (
    .LSB(in_2[8]), .in_2(in_2[9]), .in_3(in_2[10]), .MSB(in_2[11]), .out_5(out_3[10]), .out_6(out_3[26]),
    .out_7(out_4[10]), .out_8(out_4[26]));
  SBOX sbox_12 (
    .LSB(in_2[12]), .in_2(in_2[13]), .in_3(in_2[14]), .MSB(in_2[15]), .out_5(out_3[11]), .out_6(out_3[27]),
    .out_7(out_4[11]), .out_8(out_4[27]));
  SBOX sbox_13 (
    .LSB(in_2[16]), .in_2(in_2[17]), .in_3(in_2[18]), .MSB(in_2[19]), .out_5(out_3[12]), .out_6(out_3[28]),
    .out_7(out_4[12]), .out_8(out_4[28]));
  SBOX sbox_14 (
    .LSB(in_2[20]), .in_2(in_2[21]), .in_3(in_2[22]), .MSB(in_2[23]), .out_5(out_3[13]), .out_6(out_3[29]),
    .out_7(out_4[13]), .out_8(out_4[29]));
  SBOX sbox_15 (
    .LSB(in_2[24]), .in_2(in_2[25]), .in_3(in_2[26]), .MSB(in_2[27]), .out_5(out_3[14]), .out_6(out_3[30]),
    .out_7(out_4[14]), .out_8(out_4[30]));
  SBOX sbox_16 (
    .LSB(in_2[28]), .in_2(in_2[29]), .in_3(in_2[30]), .MSB(in_2[31]), .out_5(out_3[15]), .out_6(out_3[31]),
    .out_7(out_4[15]), .out_8(out_4[31]));
endmodule

module keyTRANSFORM (
  input  [4:0] in_1,
  input  [15:0] in_2,
  input  [31:0] in_3,
  input  [31:0] _48_79,
  output [15:0] out_5,
  output [31:0] out_6,
  output [31:0] out_7
);

  wire [4:0] adder_1_out;

  Adder #(.width(5)) adder_1 (.a(in_1), .b(5'b00001), .out(adder_1_out));  // open: cin, cout
  assign {out_6[3:0], out_5[15]} = in_3[22:18] ^ adder_1_out;  // XOR_Gate xor_1, 5 bits wide
  SBOX sbox_1 (
    .LSB(in_2[15]), .in_2(in_3[0]), .in_3(in_3[1]), .MSB(in_3[2]), .out_5(out_7[28]), .out_6(out_7[29]),
    .out_7(out_7[30]), .out_8(out_7[31]));

  assign out_5[14:0] = in_3[17:3];
  assign out_6[31:4] = {_48_79[18:0], in_3[31:23]};
  assign out_7[27:0] = {in_2[14:0], _48_79[31:19]};

  // Notes on the sheet:
  //   0-15
  //   16-47
endmodule

module Ramvala (
  output [31:0] out_1,
  output [31:0] out_2,
  output halt
);

  wire and_1_out, clock_1_out;
  wire [1:0] counter_1_q;
  wire [31:0] ram_1_data, ram_2_data, ram_3_data, ram_4_data, ram_5_data;

  Clock clock_1 (.out(clock_1_out));
  RAM #(.addrWidth(3), .dataWidth(32)) ram_1 (
    .addr(3'b010), .data(ram_1_data), .clk(clock_1_out));  // open: sel, ld, clr
  RAM #(.addrWidth(3), .dataWidth(32)) ram_2 (
    .addr(3'b011), .data(ram_2_data), .clk(clock_1_out));  // open: sel, ld, clr
  RAM #(.addrWidth(3), .dataWidth(32)) ram_3 (
    .addr(3'b100), .data(ram_3_data), .clk(clock_1_out));  // open: sel, ld, clr
  Counter #(.width(2), .max('h3)) counter_1 (.Q(counter_1_q), .clk(clock_1_out));  // open: load, D, count, carry, clr
  RAM #(.addrWidth(3), .dataWidth(32)) ram_4 (
    .addr(3'b000), .data(ram_4_data), .clk(clock_1_out));  // open: sel, ld, clr
  RAM #(.addrWidth(3), .dataWidth(32)) ram_5 (
    .addr(3'b001), .data(ram_5_data), .clk(clock_1_out));  // open: sel, ld, clr
  and and_1 (and_1_out, counter_1_q[1], clock_1_out);
  main main_1 (
    .in_1(and_1_out), .in_2(ram_1_data[15:0]), .in_3({ram_2_data[15:0], ram_1_data[31:16]}),
    .in_4({ram_3_data[15:0], ram_2_data[31:16]}), .in_5(ram_4_data), .in_6(ram_5_data), .out_7(halt),
    .out_8(out_1), .out_9(out_2));
endmodule
